// Logisim project Add2bits.circ as structural Verilog: 1 circuit, main circuit main
module main (
  input  A0,
  input  B0,
  input  Rp,
  input  A1,
  input  B1,
  output S0,
  output Rf,
  output S1
);

  wire and_1_out, and_2_out, and_3_out, and_4_out, or_1_out, xor_1_out, xor_3_out;

  and and_1 (and_1_out, A0, B0);
  xor xor_1 (xor_1_out, A0, B0);
  and and_2 (and_2_out, xor_1_out, Rp);
  xor xor_2 (S0, xor_1_out, Rp);
  or or_1 (or_1_out, and_1_out, and_2_out);
  and and_3 (and_3_out, A1, B1);
  xor xor_3 (xor_3_out, A1, B1);
  and and_4 (and_4_out, xor_3_out, or_1_out);
  xor xor_4 (S1, xor_3_out, or_1_out);
  or or_2 (Rf, and_3_out, and_4_out);

  // Notes on the sheet:
  //   Additionneur 2 bits complet :
endmodule
