// Logisim project Molecules.circ as structural Verilog: 1 circuit, main circuit main
module main (
  input  Diclofenac,
  input  Gefitinib,
  output out0,
  output out1,
  output out2,
  output out3,
  output out4,
  output out5,
  output out6,
  output out7
);

  wire and_2_out, and_3_out, and_5_out, and_6_out, not_1_out, not_2_out, not_3_out, not_4_out, not_5_out,
       not_6_out, not_7_out, not_8_out, not_9_out;

  not not_1 (not_1_out, Gefitinib);
  not not_2 (not_2_out, Diclofenac);
  not not_3 (not_3_out, Gefitinib);
  not not_4 (not_4_out, Gefitinib);
  not not_5 (not_5_out, Diclofenac);
  not not_6 (not_6_out, Gefitinib);
  not not_7 (not_7_out, Diclofenac);
  not not_8 (not_8_out, Diclofenac);
  not not_9 (not_9_out, Diclofenac);
  and and_1 (out0, Diclofenac, not_1_out);
  and and_2 (and_2_out, not_2_out, Gefitinib);
  and and_3 (and_3_out, Diclofenac, not_3_out);
  and and_4 (out2, Diclofenac, not_4_out);
  and and_5 (and_5_out, not_5_out, Gefitinib);
  and and_6 (and_6_out, Diclofenac, not_6_out);
  and and_7 (out5, not_7_out, Gefitinib);
  and and_8 (out6, not_8_out, Gefitinib);
  and and_9 (out7, not_9_out, Gefitinib);
  or or_1 (out1, and_2_out, and_3_out);
  or or_2 (out4, and_5_out, and_6_out);

  assign out3 = 1'b0;
endmodule
